# Fritzing sketch Untitled Sketch 2 (saved by Fritzing 0.9.2b)

parts:
  Часть2 = Arduino Uno (Rev3) - ICSP
  Часть3 = Arduino Mega 2560 (Rev3)
  PIR1 = PIR sensor
  R3 = Photocell (LDR) [package=THT]
  Часть4 = NRF24L01
  Часть5 = RF-MODULE 315/433 [package=rf-link_rx]
  U1 = RF-LINK_TX [package=rf-link_tx]
  RHT1 = Humidity and Temperature Sensor RHT03
  U2 = LM3480IM4 [package=sot23-3]
  U3 = LM3480IM4 [package=sot23-3]
  R4 = Resistor [tolerance=±5% resistance=10k package="0603 [SMD]"]
  R5 = Resistor [tolerance=±5% resistance=10k package="0603 [SMD]"]
  PIR2 = PIR sensor
  R6 = Photocell (LDR) [package=THT]
  RHT2 = Humidity and Temperature Sensor RHT03
  U4 = LM3480IM4 [package=sot23-3]
  R7 = Resistor [tolerance=±5% resistance=10k package="0603 [SMD]"]
  PIR3 = PIR sensor
  R8 = Photocell (LDR) [package=THT]
  RHT3 = Humidity and Temperature Sensor RHT03
  U5 = LM3480IM4 [package=sot23-3]
  R9 = Resistor [tolerance=±5% resistance=10k package="0603 [SMD]"]
  PIR4 = PIR sensor
  R10 = Photocell (LDR) [package=THT]
  RHT4 = Humidity and Temperature Sensor RHT03
  U6 = LM3480IM4 [package=sot23-3]

nets:
  N1: Часть2.A0, Часть4.SCK
  N2: Часть2.A1, Часть4.MOSI
  N3: Часть2.A2, Часть4.MISO
  N4: Часть2.D5_PWM, Часть4.CE
  N5: Часть2.D6_PWM, Часть4.CSN
  N6: Часть2.5V, U2.IN
  GND: Часть2.GND, Часть4.GND, U2.GND
  N7: Часть3.A8, R3.pin_0, R4.Pin_1
  N8: Часть3.A9, R5.Pin_1, R6.pin_0
  N9: Часть3.A10, R7.Pin_1, R8.pin_0
  N10: Часть3.A11, R9.Pin_1, R10.pin_0
  N11: Часть3.D21/SCL, PIR1.SIG
  N12: Часть3.D20/SDA, PIR2.SIG
  N13: Часть3.D19/RX1, PIR3.SIG
  N14: Часть3.D18/TX1, PIR4.SIG
  N15: Часть3.D26, Часть5.Data
  N16: Часть3.D28, U1.DATA
  N17: Часть3.D30, RHT1.Data-signal
  VDD: Часть3.D32, PIR2.VDD, R6.pin_1, RHT2.Vcc, RHT2.Data-signal, U4.OUT
  VDD_2: Часть3.D34, PIR3.VDD, R8.pin_1, RHT3.Vcc, RHT3.Data-signal, U5.OUT
  VDD_3: Часть3.D36, PIR4.VDD, R10.pin_1, RHT4.Vcc, RHT4.Data-signal, U6.OUT
  VDD_4: PIR1.VDD, R3.pin_1, RHT1.Vcc, U3.OUT
  GND_2: PIR1.GND, RHT1.GND_2, U3.GND, R4.Pin_0
  N18: Часть4.VCC, U2.OUT
  GND_3: Часть5.GND, U1.GND
  VCC: Часть5.VCC, U1.+5V
  GND_4: R5.Pin_0, PIR2.GND, RHT2.GND_2, U4.GND
  GND_5: R7.Pin_0, PIR3.GND, RHT3.GND_2, U5.GND
  GND_6: R9.Pin_0, PIR4.GND, RHT4.GND_2, U6.GND

custom parts:
  RF-MODULE 315/433: RF Link receivers- WRL-8947, 8948, 8949, 8950
  RF-LINK_TX: Common RF transmitter of the 315.00Mhz varity
